// Logisim project AdditionFinal.circ as structural Verilog: 5 circuits, main circuit half_adder_created
module half_adder_created (
  input  X,
  input  Y,
  output S,
  output C
);

  xor xor_1 (S, X, Y);
  and and_1 (C, X, Y);
endmodule

module Full_Adder (
  input  A,
  input  B,
  input  C,
  output Sum,
  output Carry
);

  wire and_1_out, and_2_out, xor_1_out;

  xor xor_1 (xor_1_out, A, B);
  and and_1 (and_1_out, A, B);
  and and_2 (and_2_out, xor_1_out, C);
  xor xor_2 (Sum, xor_1_out, C);
  or or_1 (Carry, and_2_out, and_1_out);
endmodule

module _2nd_complement (
  input  I0,
  input  I1,
  input  Enable,
  output O0,
  output O1
);

  wire and_1_out;

  and and_1 (and_1_out, I0, Enable);
  xor xor_1 (O1, and_1_out, I1);

  assign O0 = I0;
endmodule

module _0_to_0 (
  input  I0,
  input  I1,
  input  Sign,
  output sign_final
);

  wire or_1_out;

  or or_1 (or_1_out, I0, I1);
  and and_1 (sign_final, or_1_out, Sign);
endmodule

module Add___Subtract (
  input  Sign_A,
  input  A1,
  input  A0,
  input  Sign_B,
  input  B1,
  input  B0,
  input  OP,
  output AS,
  output A2,
  output A1_2,
  output A0_2
);

  wire and_1_out, and_3_out, and_4_out, full_adder_1_carry, full_adder_1_sum, half_adder_created_1_c,
       half_adder_created_1_s, n0_to_0_1_sign_final, n0_to_0_2_sign_final, n2nd_complement_1_o0,
       n2nd_complement_1_o1, n2nd_complement_2_o0, n2nd_complement_2_o1, nor_1_out, nor_2_out, not_1_out,
       xor_1_out, xor_2_out;

  and and_1 (and_1_out, n0_to_0_1_sign_final, not_1_out);
  nor nor_1 (nor_1_out, not_1_out, full_adder_1_carry);
  or or_1 (AS, and_1_out, nor_1_out);
  and and_2 (A2, full_adder_1_carry, not_1_out);
  _0_to_0 u_0_to_0_1 (.I0(A0), .I1(A1), .Sign(Sign_A), .sign_final(n0_to_0_1_sign_final));
  not not_1 (not_1_out, xor_1_out);
  and and_3 (and_3_out, n0_to_0_1_sign_final, xor_1_out);
  _2nd_complement u_2nd_complement_1 (
    .I0(A0), .O0(n2nd_complement_1_o0), .O1(n2nd_complement_1_o1), .I1(A1), .Enable(and_3_out));
  Full_Adder full_adder_1 (
    .A(half_adder_created_1_c), .B(n2nd_complement_1_o1), .C(n2nd_complement_2_o1), .Sum(full_adder_1_sum),
    .Carry(full_adder_1_carry));
  xor xor_1 (xor_1_out, n0_to_0_1_sign_final, n0_to_0_2_sign_final);
  nor nor_2 (nor_2_out, full_adder_1_carry, not_1_out);
  _2nd_complement u_2nd_complement_2 (
    .I0(B0), .O0(n2nd_complement_2_o0), .O1(n2nd_complement_2_o1), .I1(B1), .Enable(and_4_out));
  half_adder_created half_adder_created_1 (
    .X(n2nd_complement_2_o0), .Y(n2nd_complement_1_o0), .S(half_adder_created_1_s), .C(half_adder_created_1_c));
  _2nd_complement u_2nd_complement_3 (
    .I0(half_adder_created_1_s), .O0(A0_2), .O1(A1_2), .I1(full_adder_1_sum), .Enable(nor_2_out));
  _0_to_0 u_0_to_0_2 (.I0(B1), .I1(B0), .Sign(xor_2_out), .sign_final(n0_to_0_2_sign_final));
  and and_4 (and_4_out, xor_1_out, n0_to_0_2_sign_final);
  xor xor_2 (xor_2_out, OP, Sign_B);
endmodule
