// Logisim project MainProject.circ as structural Verilog: 5 circuits, main circuit PROJECT
module Multipler (
  input  As,
  input  A1,
  input  A0,
  input  Bs,
  input  B1,
  input  B0,
  output A0_2,
  output A1_2,
  output A2,
  output A3,
  output As_2
);

  wire and_2_out, and_3_out, and_4_out, and_5_out;

  and and_1 (A0_2, A0, B0);
  and and_2 (and_2_out, B0, A1);
  and and_3 (and_3_out, A0, B1);
  and and_4 (and_4_out, B1, A1);
  and and_5 (and_5_out, and_2_out, and_3_out);
  xor xor_1 (A1_2, and_2_out, and_3_out);
  xor xor_2 (A2, and_5_out, and_4_out);
  and and_6 (A3, and_5_out, and_4_out);
  xor xor_3 (As_2, Bs, As);
endmodule

module Multiplexer (
  input  A0,
  input  B0,
  input  A1,
  input  B1,
  input  A2,
  input  B2,
  input  A3,
  input  B3,
  input  S,
  output A0_2,
  output A1_2,
  output A2_2,
  output A3_2
);

  Multiplexer_part multiplexer_1 (.in0(A0), .in1(B0), .out(A0_2), .sel(S));  // open: en
  Multiplexer_part multiplexer_2 (.in0(A1), .in1(B1), .out(A1_2), .sel(S));  // open: en
  Multiplexer_part multiplexer_3 (.in0(A2), .in1(B2), .out(A2_2), .sel(S));  // open: en
  Multiplexer_part multiplexer_4 (.in0(A3), .in1(B3), .out(A3_2), .sel(S));  // open: en
endmodule

module ALU (
  input  A0,
  input  A1,
  input  AS,
  input  B0,
  input  B1,
  input  BS,
  input  OP1,
  input  OP0,
  output Equals_0_LED,
  output D,
  output C,
  output B,
  output Sign_Segment,
  output A,
  output Div_By__0_LED
);

  wire add_subtract_1_a0_2, add_subtract_1_a1_2, add_subtract_1_a2, add_subtract_1_as, modulus_1_a0_2,
       modulus_1_a1_2, modulus_1_a2, modulus_1_as, modulus_1_div_by_0, multipler_1_a0_2, multipler_1_a1_2,
       multipler_1_a2, multipler_1_a3, multipler_1_as_2, multiplexer_1_a0_2, multiplexer_1_a1_2,
       multiplexer_1_a2_2, multiplexer_1_a3_2, multiplexer_3_out, multiplexer_4_out, or_1_out;

  Add___Subtract add_subtract_1 (
    .OP(OP0), .Sign_A(AS), .A1(A1), .A0(A0), .Sign_B(BS), .B1(B1), .B0(B0), .AS(add_subtract_1_as),
    .A2(add_subtract_1_a2), .A1_2(add_subtract_1_a1_2), .A0_2(add_subtract_1_a0_2));
  Multipler multipler_1 (
    .As(BS), .A1(B1), .A0(B0), .Bs(AS), .B1(A1), .B0(A0), .A0_2(multipler_1_a0_2), .A1_2(multipler_1_a1_2),
    .A2(multipler_1_a2), .A3(multipler_1_a3), .As_2(multipler_1_as_2));
  Modulus modulus_1 (
    .A_Sign(AS), .A0(A0), .A1(A1), .B0(B0), .B1(B1), .As(modulus_1_as), .A0_2(modulus_1_a0_2),
    .A1_2(modulus_1_a1_2), .A2(modulus_1_a2), .Div_By_0(modulus_1_div_by_0));
  Multiplexer multiplexer_1 (
    .A0(multipler_1_a0_2), .B0(modulus_1_a0_2), .A1(multipler_1_a1_2), .B1(modulus_1_a1_2),
    .A2(multipler_1_a2), .B2(modulus_1_a2), .A3(multipler_1_a3), .B3(1'b0), .S(OP0),
    .A0_2(multiplexer_1_a0_2), .A1_2(multiplexer_1_a1_2), .A2_2(multiplexer_1_a2_2), .A3_2(multiplexer_1_a3_2));
  Multiplexer multiplexer_2 (
    .A0(add_subtract_1_a0_2), .B0(multiplexer_1_a0_2), .A1(add_subtract_1_a1_2), .B1(multiplexer_1_a1_2),
    .A2(add_subtract_1_a2), .B2(multiplexer_1_a2_2), .A3(1'b0), .B3(multiplexer_1_a3_2), .S(OP1), .A0_2(A),
    .A1_2(B), .A2_2(C), .A3_2(D));
  Multiplexer_part #(.enable("false")) multiplexer_3 (
    .in0(multipler_1_as_2), .in1(modulus_1_as), .out(multiplexer_3_out), .sel(OP0));
  or or_1 (or_1_out, A, B, C, D);
  Multiplexer_part #(.enable("false")) multiplexer_4 (
    .in0(add_subtract_1_as), .in1(multiplexer_3_out), .out(multiplexer_4_out), .sel(OP1));
  and and_1 (Div_By__0_LED, modulus_1_div_by_0, OP1, OP0);
  not not_1 (Equals_0_LED, or_1_out);
  and and_2 (Sign_Segment, or_1_out, multiplexer_4_out);
endmodule

module PROJECT (
  input  AS,
  input  A1,
  input  A0,
  input  BS,
  input  B1,
  input  B0,
  input  OP1,
  input  OP0
);

  wire ALU_a, ALU_b, ALU_c, ALU_d, ALU_div_by__0_led, ALU_equals_0_led, ALU_sign_segment, and_1_out,
       n7_segment_display_driver_1_a_2, n7_segment_display_driver_1_b_2, n7_segment_display_driver_1_c_2,
       n7_segment_display_driver_1_d_2, n7_segment_display_driver_1_e, n7_segment_display_driver_1_f,
       n7_segment_display_driver_1_g, not_1_out;

  ALU ALU (
    .A0(A0), .A1(A1), .B0(B0), .B1(B1), .BS(BS), .OP1(OP1), .OP0(OP0), .Equals_0_LED(ALU_equals_0_led),
    .D(ALU_d), .C(ALU_c), .B(ALU_b), .A(ALU_a), .Div_By__0_LED(ALU_div_by__0_led),
    .Sign_Segment(ALU_sign_segment), .AS(AS));
  not not_1 (not_1_out, ALU_div_by__0_led);
  _7_segment_display_driver u_7_segment_display_driver_1 (
    .D(ALU_d), .C(ALU_c), .B(ALU_b), .A(ALU_a), .VCC(not_1_out), .a_2(n7_segment_display_driver_1_a_2),
    .b_2(n7_segment_display_driver_1_b_2), .c_2(n7_segment_display_driver_1_c_2),
    .d_2(n7_segment_display_driver_1_d_2), .e(n7_segment_display_driver_1_e),
    .f(n7_segment_display_driver_1_f), .g(n7_segment_display_driver_1_g));
  and and_1 (and_1_out, not_1_out, ALU_equals_0_led);
  _7_Segment_Display u_7_segment_display_1 (
    .g(n7_segment_display_driver_1_g), .f(n7_segment_display_driver_1_f),
    .a(n7_segment_display_driver_1_a_2), .b(n7_segment_display_driver_1_b_2),
    .e(n7_segment_display_driver_1_e), .d(n7_segment_display_driver_1_d_2),
    .c(n7_segment_display_driver_1_c_2));  // open: dp
  _7_Segment_Display u_7_segment_display_2 (.g(ALU_sign_segment));  // open: f, a, b, e, d, c, dp
  LED Div_By_0 (.in(ALU_div_by__0_led));
  LED _0_OUTPUT (.in(and_1_out));
endmodule

module _7_segment_display_driver (
  input  D,
  input  C,
  input  B,
  input  A,
  input  VCC,
  output a_2,
  output b_2,
  output c_2,
  output d_2,
  output e,
  output f,
  output g
);

  wire and_1_out, and_2_out, and_3_out, and_4_out, and_5_out, and_6_out, and_7_out, and_8_out, and_9_out,
       and_10_out, and_11_out, and_12_out, and_13_out, and_14_out, and_15_out, and_16_out, and_17_out,
       and_18_out, and_19_out, and_20_out, and_21_out, and_22_out, and_23_out, and_24_out, and_25_out,
       and_26_out, and_27_out, and_28_out, and_29_out, and_30_out, and_31_out, and_32_out, and_33_out,
       and_34_out, and_35_out, not_1_out, not_2_out, not_3_out, not_4_out, not_5_out, not_6_out, not_7_out,
       not_8_out, not_9_out, not_10_out, not_11_out, not_12_out, not_13_out, not_14_out, not_15_out,
       not_16_out, not_17_out, not_18_out, not_19_out, not_20_out, not_21_out, not_22_out, not_23_out,
       not_24_out, not_25_out, not_26_out, not_27_out, not_28_out, not_29_out, not_30_out, not_31_out,
       not_32_out, not_33_out, not_34_out, not_35_out, not_36_out, not_37_out, not_38_out, not_39_out,
       not_40_out, not_41_out, not_42_out, not_43_out, not_44_out;

  not not_1 (not_1_out, C);
  not not_2 (not_2_out, A);
  not not_3 (not_3_out, D);
  not not_4 (not_4_out, D);
  not not_5 (not_5_out, C);
  not not_6 (not_6_out, B);
  not not_7 (not_7_out, A);
  not not_8 (not_8_out, D);
  not not_9 (not_9_out, C);
  not not_10 (not_10_out, D);
  not not_11 (not_11_out, B);
  not not_12 (not_12_out, A);
  not not_13 (not_13_out, C);
  not not_14 (not_14_out, A);
  not not_15 (not_15_out, D);
  not not_16 (not_16_out, B);
  not not_17 (not_17_out, D);
  not not_18 (not_18_out, B);
  not not_19 (not_19_out, D);
  not not_20 (not_20_out, B);
  not not_21 (not_21_out, D);
  not not_22 (not_22_out, C);
  not not_23 (not_23_out, D);
  not not_24 (not_24_out, C);
  not not_25 (not_25_out, A);
  not not_26 (not_26_out, C);
  not not_27 (not_27_out, B);
  not not_28 (not_28_out, A);
  not not_29 (not_29_out, B);
  not not_30 (not_30_out, A);
  not not_31 (not_31_out, C);
  not not_32 (not_32_out, A);
  not not_33 (not_33_out, A);
  not not_34 (not_34_out, B);
  not not_35 (not_35_out, A);
  not not_36 (not_36_out, D);
  not not_37 (not_37_out, B);
  not not_38 (not_38_out, A);
  not not_39 (not_39_out, C);
  not not_40 (not_40_out, C);
  not not_41 (not_41_out, A);
  not not_42 (not_42_out, D);
  not not_43 (not_43_out, B);
  not not_44 (not_44_out, C);
  and and_1 (and_1_out, VCC, not_1_out, not_2_out);
  and and_2 (and_2_out, VCC, not_3_out, B);
  and and_3 (and_3_out, VCC, not_4_out, C, A);
  and and_4 (and_4_out, VCC, C, B);
  and and_5 (and_5_out, VCC, D, not_5_out, not_6_out);
  and and_6 (and_6_out, VCC, D, not_7_out);
  and and_7 (and_7_out, VCC, not_8_out, not_9_out);
  and and_8 (and_8_out, VCC, not_10_out, not_11_out, not_12_out);
  and and_9 (and_9_out, VCC, not_13_out, not_14_out);
  and and_10 (and_10_out, VCC, not_15_out, B, A);
  and and_11 (and_11_out, VCC, D, not_16_out, A);
  and and_12 (and_12_out, VCC, not_17_out, not_18_out);
  and and_13 (and_13_out, VCC, not_19_out, A);
  and and_14 (and_14_out, VCC, not_20_out, A);
  and and_15 (and_15_out, VCC, not_21_out, C);
  and and_16 (and_16_out, VCC, D, not_22_out);
  and and_17 (and_17_out, VCC, not_23_out, not_24_out, not_25_out);
  and and_18 (and_18_out, VCC, not_26_out, B, A);
  and and_19 (and_19_out, VCC, C, not_27_out, A);
  and and_20 (and_20_out, VCC, C, B, not_28_out);
  and and_21 (and_21_out, VCC, D, not_29_out, not_30_out);
  and and_22 (and_22_out, VCC, not_31_out, not_32_out);
  and and_23 (and_23_out, VCC, B, not_33_out);
  and and_24 (and_24_out, VCC, D, B);
  and and_25 (and_25_out, VCC, D, C);
  and and_26 (and_26_out, VCC, not_34_out, not_35_out);
  and and_27 (and_27_out, VCC, not_36_out, C, not_37_out);
  and and_28 (and_28_out, VCC, C, not_38_out);
  and and_29 (and_29_out, VCC, D, not_39_out);
  and and_30 (and_30_out, VCC, D, B);
  and and_31 (and_31_out, VCC, not_40_out, B);
  and and_32 (and_32_out, VCC, B, not_41_out);
  and and_33 (and_33_out, VCC, not_42_out, C, not_43_out);
  and and_34 (and_34_out, VCC, D, not_44_out);
  and and_35 (and_35_out, VCC, D, A);
  or or_1 (a_2, and_1_out, and_2_out, and_3_out, and_4_out, and_5_out, and_6_out);
  or or_2 (b_2, and_7_out, and_8_out, and_9_out, and_10_out, and_11_out);
  or or_3 (c_2, and_12_out, and_13_out, and_14_out, and_15_out, and_16_out);
  or or_4 (d_2, and_17_out, and_18_out, and_19_out, and_20_out, and_21_out);
  or or_5 (e, and_22_out, and_23_out, and_24_out, and_25_out);
  or or_6 (f, and_26_out, and_27_out, and_28_out, and_29_out, and_30_out);
  or or_7 (g, and_31_out, and_32_out, and_33_out, and_34_out, and_35_out);
endmodule
