// Logisim project ModulusProject.circ as structural Verilog: 1 circuit, main circuit Modulus
module Modulus (
  input  A_Sign,
  input  A0,
  input  A1,
  input  B0,
  input  B1,
  output As,
  output A0_2,
  output A1_2,
  output A2,
  output Div_By_0
);

  wire nand_1_out, not_1_out, or_1_out;

  not not_1 (not_1_out, A0);
  nand nand_1 (nand_1_out, A1, B0);
  nor nor_1 (Div_By_0, B0, B1);
  and and_1 (A0_2, A0, nand_1_out, B1);
  and and_2 (A1_2, not_1_out, A1, B0, B1);
  or or_1 (or_1_out, A0_2, A1_2);
  and and_3 (As, or_1_out, A_Sign);

  assign A2 = 1'b0;
endmodule
