// Logisim project MultiplerProject.circ as structural Verilog: 3 circuits, main circuit Multipler
module Multipler (
  input  As,
  input  A1,
  input  A0,
  input  Bs,
  input  B1,
  input  B0,
  output out_7,
  output out_8,
  output out_9,
  output out_10,
  output out_11
);

  wire and_2_out, and_3_out, and_4_out, and_5_out;

  and and_1 (out_7, A0, B0);
  and and_2 (and_2_out, B0, A1);
  and and_3 (and_3_out, A0, B1);
  and and_4 (and_4_out, B1, A1);
  and and_5 (and_5_out, and_2_out, and_3_out);
  xor xor_1 (out_8, and_2_out, and_3_out);
  xor xor_2 (out_9, and_5_out, and_4_out);
  and and_6 (out_10, and_5_out, and_4_out);
  xor xor_3 (out_11, Bs, As);
endmodule

module Main (
  input  A0,
  input  A1,
  input  AS,
  input  B0,
  input  B1,
  input  BS,
  input  OP1,
  input  OP0
);

  Multipler multipler_1 (
    .As(BS), .A1(B1), .A0(B0), .Bs(AS), .B1(A1), .B0(A0));  // open: out_7, out_8, out_9, out_10, out_11
  // ModulusProject_main main_1: pin names not known; wires that end beside it: AS, A0, A1, B0, B1
endmodule

module Multiplexer (
  input  A0,
  input  B0,
  input  A1,
  input  B1,
  input  A2,
  input  B2,
  input  A3,
  input  B3,
  input  S,
  output A0_2,
  output A1_2,
  output A2_2,
  output A3_2
);

  Multiplexer_part multiplexer_1 (.in0(A0), .in1(B0), .out(A0_2), .sel(S));  // open: en
  Multiplexer_part multiplexer_2 (.in0(A1), .in1(B1), .out(A1_2), .sel(S));  // open: en
  Multiplexer_part multiplexer_3 (.in0(A2), .in1(B2), .out(A2_2), .sel(S));  // open: en
  Multiplexer_part multiplexer_4 (.in0(A3), .in1(B3), .out(A3_2), .sel(S));  // open: en
endmodule
